# Fritzing sketch NixiePad (saved by Fritzing 0.9.2b)
circuit board: 3.61968cm x 2.53067cm
breadboards: 1

parts:
  Part1 = IN-14 nixie tube [part_number=IN-14 package=THT]
  U1 = HV5522PG [part_number=HV5522PG package=tqfp44]

nets:
  N1: Part1.pinPL, U1.HV1
  N2: Part1.pin1, U1.HV2
  N3: Part1.pin2, U1.HV3
  N4: Part1.pin3, U1.HV4
  N5: Part1.pin4, U1.HV5
  N6: Part1.pin5, U1.HV6
  N7: Part1.pin6, U1.HV7
  N8: Part1.pin7, U1.HV8
  N9: Part1.pin8, U1.HV9
  N10: Part1.pin9, U1.HV10
  N11: Part1.pin0, U1.HV11
  N12: Part1.pinPR, U1.HV12

custom parts:
  IN-14 nixie tube: IN-14 nixie tube footprint
  HV5522PG: High-Voltage Driver Chip (Open-Drain)
