# Fritzing sketch Riser (saved by Fritzing 0.9.2b)
circuit board: 4.20073cm x 2.56974cm
breadboards: 1

parts:
  Part1 = IN-14 nixie tube [part_number=IN-14 package=THT]
  Part2 = IN-14 nixie tube [part_number=IN-14 package=THT]
  Adapter1 = Nixie Tube Riser [package="DIP (Dual Inline) [THT]"]

nets:
  N1: Part1.Anode, Adapter1.+L
  N2: Part1.pinPL, Adapter1.R.L
  N3: Part1.pin1, Adapter1.1L
  N4: Part1.pin2, Adapter1.2L
  N5: Part1.pin3, Adapter1.3L
  N6: Part1.pin4, Adapter1.4L
  N7: Part1.pin5, Adapter1.5L
  N8: Part1.pin6, Adapter1.6L
  N9: Part1.pin7, Adapter1.7L
  N10: Part1.pin8, Adapter1.8L
  N11: Part1.pin9, Adapter1.9L
  N12: Part1.pin0, Adapter1.0L
  N13: Part1.pinPR, Adapter1.L.L
  N14: Part2.Anode, Adapter1.+R
  N15: Part2.pinPL, Adapter1.R.R
  N16: Part2.pin1, Adapter1.1R
  N17: Part2.pin2, Adapter1.2R
  N18: Part2.pin3, Adapter1.3R
  N19: Part2.pin4, Adapter1.4R
  N20: Part2.pin5, Adapter1.5R
  N21: Part2.pin6, Adapter1.6R
  N22: Part2.pin7, Adapter1.7R
  N23: Part2.pin8, Adapter1.8R
  N24: Part2.pin9, Adapter1.9R
  N25: Part2.pin0, Adapter1.0R
  N26: Part2.pinPR, Adapter1.L.R

custom parts:
  IN-14 nixie tube: IN-14 nixie tube footprint
  Nixie Tube Riser: A riser to lift nixie tubes from the underlying board.
